# Fritzing sketch electro (saved by Fritzing 0.9.2b)
breadboards: 3

parts:
  Part1 = Photon  # not connected
  R1 = Resistor [tolerance=±5% resistance=220 package=THT]
  R2 = Resistor [tolerance=±5% resistance=220 package=THT]

nets:
  N1: R1.Pin_1, R2.Pin_0
